// Logisim project NAND2Tetris_CPU.circ as structural Verilog: 1 circuit, main circuit CPU-2
module CPU_2 (
  input  [15:0] inM,
  input  [15:0] instruction,
  input  reset,
  output [15:0] outM,
  output writeM,
  output [14:0] addressM,
  output [15:0] pc
);

  wire alu_1_zr, JMP, nor_1_out, not_1_out, TICK;
  wire [15:0] A_q, and_1_out, demultiplexer_1_out0;

  Clock clock_1 (.out(TICK));
  Demultiplexer #(.width(16), .enable("false")) demultiplexer_1 (
    .out0(demultiplexer_1_out0), .in(instruction), .sel(instruction[15]));  // open: out1
  assign and_1_out = 16'h7fff & demultiplexer_1_out0;  // AND_Gate and_1, 16 bits wide
  nor nor_1 (nor_1_out, instruction[2], instruction[1], instruction[0]);
  Register #(.width(16)) A (.D(and_1_out), .Q(A_q), .clk(TICK));  // open: en, clr
  Counter #(.width(16), .max('hffff)) u_PC (
    .load(JMP), .D(A_q), .count(nor_1_out), .Q(pc), .clk(TICK), .clr(reset));  // open: carry
  Register #(.width(16)) D ();  // open: D, en, Q, clk, clr
  and and_2 (JMP, alu_1_zr, instruction[1]);
  not not_1 (not_1_out, nor_1_out);
  ALU alu_1 (.x(A_q), .zy(nor_1_out), .ny(not_1_out), .f(nor_1_out), .zr(alu_1_zr));  // open: y, zx, nx, no, out, ng
endmodule
