// Logisim project TestALU.circ as structural Verilog: 1 circuit, main circuit main
module main (
  input  in_1,
  input  in_2,
  input  in_3,
  input  in_4,
  input  in_5,
  input  in_6,
  output [15:0] out_7
);

  ALU alu_1 (
    .x(16'h3), .y({16{1'b1}}), .zx(in_3), .nx(in_4), .zy(in_5), .ny(in_6), .f(in_1), .no(in_2), .out(out_7));  // open: zr, ng
  // Probe on out_7
endmodule
